# Fritzing sketch TrafficLight (saved by Fritzing 0.8.7b)
breadboards: 1

parts:
  元件1 = Arduino Uno (Rev3)
  LED1 = LED - 5mm [color="Red (633nm)" package="5 mm [THT]"]
  LED2 = LED - 5mm [color="Green (565nm)" package="5 mm [THT]"]
  LED3 = LED - 5mm [color="Yellow (574nm)" package="5 mm [THT]"]

nets:
  N1: 元件1.D2, 元件1.GND, LED1.cathode, LED2.anode, LED3.anode
  N2: 元件1.D3_PWM, LED2.cathode
  N3: 元件1.D4, LED3.cathode
